# Fritzing sketch Task1.1P_Diagram (saved by Fritzing 0.9.3b)
breadboards: 1

parts:
  Part1 = Arduino Mega 2560 (Rev3)
  R1 = PHOTOCELL [package=photocell]  # not connected
  R2 = Resistor [tolerance=±5% resistance=220 package=THT]
  LED1 = smd LED [color="Red (633nm)" package="1206 [SMD]"]
  R3 = Resistor [tolerance=±5% resistance=220 package=THT]

nets:
  N1: Part1.A0, R2.Pin_0
  N2: Part1.GND, R2.Pin_1, R3.Pin_1
  N3: Part1.D13_PWM, LED1.anode
  N4: LED1.cathode, R3.Pin_0
